// Logisim project cpu.circ as structural Verilog: 3 circuits, main circuit main
module main (
  input  [15:0] INSTRUCTION,
  input  CLOCK,
  output [15:0] FETCH_ADDRESS,
  output Overflow,
  output [15:0] s0_Value,
  output [15:0] s1_Value,
  output [15:0] s2_Value,
  output [15:0] ra_Value,
  output [15:0] sp_Value,
  output [15:0] HI_Value,
  output [15:0] LO_Value
);

  wire Equal, MEM_p1, MEM_p4, MEM_p7, MEM_p10, MEM_p13, MEM_p16;

  Register #(.width(16)) PC ();  // open: D, en, Q, clk, clr
  Register #(.width(16)) HI ();  // open: D, en, Q, clk, clr
  Register #(.width(16)) LO ();  // open: D, en, Q, clk, clr
  // regfile_main main_1: pin names not known
  alu_main main_2 (.Equal(Equal));  // open: Switch, X, Result, Y, Result_2, Signed_Overflow
  // mem_main MEM: pin names not known; wires that end beside it: MEM_p1, MEM_p1, s2_Value, MEM_p4, MEM_p4, ra_Value, MEM_p7, MEM_p7, sp_Value, MEM_p10, MEM_p10, HI_Value, MEM_p13, MEM_p13, LO_Value, MEM_p16

  // Other names for the same wires on the sheet: clk = CLOCK; fetch_addr[15:0] = FETCH_ADDRESS

  // Notes on the sheet:
  //   Output
  //   These are outputs/inputs from run.circ
  //   Inputs
  //   These are DEBUG/TEST outputs from your circuit.
endmodule

module Control_signal (
  input  [15:0] Input,
  output lui,
  output Mult,
  output R,
  output RegWr,
  output Jump,
  output Branch,
  output ExtOp,
  output AluSrc,
  output MemWrite,
  output MemToReg,
  output [2:0] AluCtr,
  output U_RegDst
);

  wire addi, addiu, andi, beq, bne, j, jr, lh, mfhi, mflo, or_4_out, ori, slti;
  wire [2:0] AluCtr_not_R;

  Multiplexer #(.select(4), .width(3)) multiplexer_1 (
    .in6(3'b010), .in7(3'b101), .in8(3'b110), .in9(3'b011), .in10(3'b100), .out(AluCtr_not_R),
    .sel(Input[15:12]));  // open: in0, in1, in2, in3, in4, in5, in11, in12, in13, in14, in15, en
  and isRtype (R, ~Input[12], ~Input[13], ~Input[14], ~Input[15]);  // AND_Gate
  and and_1 (lui, Input[12], ~Input[13], ~Input[14], ~Input[15]);  // AND_Gate
  and and_2 (beq, ~Input[15], Input[14], ~Input[13], ~Input[12]);  // AND_Gate
  and and_3 (j, ~Input[15], ~Input[14], Input[13], ~Input[12]);  // AND_Gate
  and and_4 (addi, ~Input[15], Input[14], Input[13], ~Input[12]);  // AND_Gate
  and and_5 (addiu, ~Input[15], Input[14], Input[13], Input[12]);  // AND_Gate
  and and_6 (slti, Input[15], ~Input[14], ~Input[13], ~Input[12]);  // AND_Gate
  and and_7 (Mult, Input[2], Input[1], Input[0]);
  and and_8 (mfhi, Input[15], Input[14], ~Input[13], Input[12]);  // AND_Gate
  and and_9 (mflo, Input[15], Input[14], Input[13], ~Input[12]);  // AND_Gate
  and and_10 (andi, Input[15], ~Input[14], ~Input[13], Input[12]);  // AND_Gate
  and and_11 (ori, Input[15], ~Input[14], Input[13], ~Input[12]);  // AND_Gate
  and and_12 (lh, Input[15], ~Input[14], Input[13], Input[12]);  // AND_Gate
  and and_13 (MemWrite, Input[15], Input[14], ~Input[13], ~Input[12]);  // AND_Gate
  and and_14 (bne, ~Input[15], Input[14], ~Input[13], Input[12]);  // AND_Gate
  and and_15 (jr, ~Input[15], ~Input[14], Input[13], Input[13]);  // AND_Gate
  Multiplexer #(.width(3)) multiplexer_2 (.in0(AluCtr_not_R), .in1(Input[2:0]), .out(AluCtr), .sel(R));  // open: en
  or or_1 (RegWr, R, lui, addi, addiu, mfhi, mflo, ori, lh);
  or or_2 (Jump, j, jr);
  or or_3 (Branch, beq, bne);
  or or_4 (or_4_out, andi, ori);
  not not_1 (ExtOp, or_4_out);
  or or_5 (AluSrc, addi, ori, lh, andi, MemWrite, addiu);
  or or_6 (MemToReg, mflo, mfhi, lh);
  or or_7 (U_RegDst, j, lui);

  // Other names for the same wires on the sheet: sh = MemWrite

  // Notes on the sheet:
  //   sll
  //   addi
  //   and
  //   or
  //   addiu
  //   slti
endmodule

module PC (
  input  [15:0] R_s__Signext_imm,
  input  [15:0] in_2,
  input  [9:0] J_imm,
  input  [5:0] imm,
  input  [3:0] opcode,
  input  equal,
  input  Jump,
  input  U,
  output [15:0] PC_2,
  output [15:0] Jump_Address,
  output [15:0] PC___SignExt_imm,
  output [15:0] NextPC,
  output Branch_Taken
);

  wire and_1_out, and_2_out, and_3_out, and_4_out, comparator_1_eq, comparator_2_eq;
  wire [15:0] bit_extender_1_out, bit_extender_2_out, bit_extender_3_out, multiplexer_1_out,
       multiplexer_2_out, shifter_1_out;

  Adder #(.width(16)) adder_1 (.a(16'h2), .b(in_2), .out(PC_2));  // open: cin, cout
  assign bit_extender_1_out = {{10{1'b0}}, in_2[15:10]};  // Bit_Extender bit_extender_1
  assign bit_extender_2_out = {{10{imm[5]}}, imm};  // Bit_Extender bit_extender_2
  Comparator #(.width(4)) comparator_1 (.a(opcode), .b(4'b0100), .eq(comparator_1_eq));  // open: gt, lt
  Comparator #(.width(4)) comparator_2 (.a(opcode), .b(4'b0101), .eq(comparator_2_eq));  // open: gt, lt
  Shifter #(.width(16)) shifter_1 (.in(bit_extender_1_out), .\dist (4'b1010), .out(shifter_1_out));
  Adder #(.width(16)) adder_2 (.a(in_2), .b(bit_extender_2_out), .out(PC___SignExt_imm));  // open: cin, cout
  and and_1 (and_1_out, comparator_1_eq, equal);
  and and_2 (and_2_out, comparator_2_eq, ~equal);  // AND_Gate
  assign bit_extender_3_out = {{6{1'b0}}, J_imm};  // Bit_Extender bit_extender_3
  Multiplexer #(.width(16)) multiplexer_1 (
    .in0(PC_2), .in1(PC___SignExt_imm), .out(multiplexer_1_out), .sel(Branch_Taken));  // open: en
  or or_1 (Branch_Taken, and_1_out, and_2_out);
  Adder #(.width(16)) adder_3 (.a(shifter_1_out), .b(bit_extender_3_out), .out(Jump_Address));  // open: cin, cout
  Multiplexer #(.width(16)) multiplexer_2 (
    .in0(multiplexer_1_out), .in1(Jump_Address), .out(multiplexer_2_out), .sel(and_3_out));  // open: en
  and and_3 (and_3_out, Jump, U);
  Multiplexer #(.width(16)) multiplexer_3 (
    .in0(multiplexer_2_out), .in1(R_s__Signext_imm), .out(NextPC), .sel(and_4_out));  // open: en
  and and_4 (and_4_out, Jump, ~U);  // AND_Gate

  // Other names for the same wires on the sheet: J_address[15:0] = Jump_Address; next_PC[15:0] = NextPC;
  //   PC_Signext_imm[15:0] = PC___SignExt_imm

  // Notes on the sheet:
  //   PC
endmodule
